// Logisim project ENIGMA.circ as structural Verilog
module FLIP_FLOP (
  input  in_1,
  input  in_2,
  output out_3
);

  wire latch_d_1_q;

  LATCH_D latch_d_1 (.D(in_1), .CLK(in_2), .Q(latch_d_1_q));  // open: nQ
  LATCH_D latch_d_2 (.D(latch_d_1_q), .CLK(in_2), .Q(out_3));  // open: nQ
endmodule

module LATCH_D (
  input  D,
  input  CLK,
  output nQ,
  output Q
);

  wire and_1_out, and_2_out;

  and and_1 (and_1_out, D, CLK);
  and and_2 (and_2_out, CLK, ~D);  // AND_Gate
  nor nor_1 (nQ, and_1_out, Q);
  nor nor_2 (Q, nQ, and_2_out);
endmodule

module NEXTINDEX_FORWARD (
  input  [4:0] INPUT_INDEX,
  input  [4:0] INPUT_ROTOR,
  output [4:0] SHIFT_INDEX
);

  wire comparator_1_lt;
  wire [4:0] subtractor_1_out, subtractor_2_out;

  Subtractor #(.width(5)) subtractor_1 (.a(INPUT_INDEX), .b(INPUT_ROTOR), .out(subtractor_1_out));  // open: bin, bout
  Comparator #(.width(5), .mode("unsigned")) comparator_1 (
    .a(INPUT_INDEX), .b(INPUT_ROTOR), .lt(comparator_1_lt));  // open: gt, eq
  Subtractor #(.width(5)) subtractor_2 (.a(subtractor_1_out), .b(5'b00110), .out(subtractor_2_out));  // open: bin, bout
  Multiplexer #(.width(5), .enable("false")) multiplexer_1 (
    .in0(subtractor_1_out), .in1(subtractor_2_out), .out(SHIFT_INDEX), .sel(comparator_1_lt));
endmodule

module ROTOR_A (
  input  INPUT_1,
  input  [25:0] INPUT_26_LETTERS,
  input  [4:0] ROTOR_POSITION,
  input  [25:0] INPUT_26_LETTERS_2,
  output OUTPUT_1,
  output [25:0] OUTPUT_26_LETTERS,
  output [25:0] OUTPUT_26_LETTERS_2
);

  wire demultiplexer_1_out26, demultiplexer_2_out26, demultiplexer_3_out26, demultiplexer_4_out26;
  wire [4:0] bitfinder_1_index, bitfinder_2_index, bitfinder_3_index, bitfinder_4_index,
       nextindex_backward_1_shift_index, nextindex_backward_2_shift_index, nextindex_forward_1_shift_index,
       nextindex_forward_2_shift_index;
  wire [25:0] demultiplexer_3_out5, demultiplexer_4_out5;

  Demultiplexer #(.select(5), .enable("false")) demultiplexer_1 (
    .out0(OUTPUT_26_LETTERS[0]), .out1(OUTPUT_26_LETTERS[1]), .out2(OUTPUT_26_LETTERS[2]),
    .out3(OUTPUT_26_LETTERS[3]), .out4(OUTPUT_26_LETTERS[4]), .out5(OUTPUT_26_LETTERS[5]),
    .out6(OUTPUT_26_LETTERS[6]), .out7(OUTPUT_26_LETTERS[7]), .out8(OUTPUT_26_LETTERS[8]),
    .out9(OUTPUT_26_LETTERS[9]), .out10(OUTPUT_26_LETTERS[10]), .out11(OUTPUT_26_LETTERS[11]),
    .out12(OUTPUT_26_LETTERS[12]), .out13(OUTPUT_26_LETTERS[13]), .out14(OUTPUT_26_LETTERS[14]),
    .out15(OUTPUT_26_LETTERS[15]), .out16(OUTPUT_26_LETTERS[16]), .out17(OUTPUT_26_LETTERS[17]),
    .out18(OUTPUT_26_LETTERS[18]), .out19(OUTPUT_26_LETTERS[19]), .out20(OUTPUT_26_LETTERS[20]),
    .out21(OUTPUT_26_LETTERS[21]), .out22(OUTPUT_26_LETTERS[22]), .out23(OUTPUT_26_LETTERS[23]),
    .out24(OUTPUT_26_LETTERS[24]), .out25(OUTPUT_26_LETTERS[25]), .out26(demultiplexer_1_out26),
    .out27(demultiplexer_1_out26), .out28(demultiplexer_1_out26), .out29(demultiplexer_1_out26),
    .out30(demultiplexer_1_out26), .out31(demultiplexer_1_out26), .in(INPUT_1),
    .sel(nextindex_backward_1_shift_index));
  Demultiplexer #(.select(5), .enable("false")) demultiplexer_2 (
    .out0(OUTPUT_26_LETTERS_2[0]), .out1(OUTPUT_26_LETTERS_2[1]), .out2(OUTPUT_26_LETTERS_2[2]),
    .out3(OUTPUT_26_LETTERS_2[3]), .out4(OUTPUT_26_LETTERS_2[4]), .out5(OUTPUT_26_LETTERS_2[5]),
    .out6(OUTPUT_26_LETTERS_2[6]), .out7(OUTPUT_26_LETTERS_2[7]), .out8(OUTPUT_26_LETTERS_2[8]),
    .out9(OUTPUT_26_LETTERS_2[9]), .out10(OUTPUT_26_LETTERS_2[10]), .out11(OUTPUT_26_LETTERS_2[11]),
    .out12(OUTPUT_26_LETTERS_2[12]), .out13(OUTPUT_26_LETTERS_2[13]), .out14(OUTPUT_26_LETTERS_2[14]),
    .out15(OUTPUT_26_LETTERS_2[15]), .out16(OUTPUT_26_LETTERS_2[16]), .out17(OUTPUT_26_LETTERS_2[17]),
    .out18(OUTPUT_26_LETTERS_2[18]), .out19(OUTPUT_26_LETTERS_2[19]), .out20(OUTPUT_26_LETTERS_2[20]),
    .out21(OUTPUT_26_LETTERS_2[21]), .out22(OUTPUT_26_LETTERS_2[22]), .out23(OUTPUT_26_LETTERS_2[23]),
    .out24(OUTPUT_26_LETTERS_2[24]), .out25(OUTPUT_26_LETTERS_2[25]), .out26(demultiplexer_2_out26),
    .out27(demultiplexer_2_out26), .out28(demultiplexer_2_out26), .out29(demultiplexer_2_out26),
    .out30(demultiplexer_2_out26), .out31(demultiplexer_2_out26), .in(INPUT_1),
    .sel(nextindex_forward_1_shift_index));
  BitFinder #(.width(26)) bitfinder_1 (.in(demultiplexer_3_out5), .index(bitfinder_1_index));  // open: found
  NEXTINDEX_BACKWARD nextindex_backward_1 (
    .INPUT_ROTOR(ROTOR_POSITION), .SHIFT_INDEX(nextindex_backward_1_shift_index),
    .INPUT_INDEX(bitfinder_1_index));
  BitFinder #(.width(26)) bitfinder_2 (.in(demultiplexer_4_out5), .index(bitfinder_2_index));  // open: found
  NEXTINDEX_FORWARD nextindex_forward_1 (
    .INPUT_INDEX(bitfinder_2_index), .INPUT_ROTOR(ROTOR_POSITION),
    .SHIFT_INDEX(nextindex_forward_1_shift_index));
  Demultiplexer #(.select(5), .enable("false")) demultiplexer_3 (
    .out0(demultiplexer_3_out5[5]), .out1(demultiplexer_3_out5[9]), .out2(demultiplexer_3_out5[24]),
    .out3(demultiplexer_3_out5[15]), .out4(demultiplexer_3_out5[7]), .out5(demultiplexer_3_out5[0]),
    .out6(demultiplexer_3_out5[21]), .out7(demultiplexer_3_out5[25]), .out8(demultiplexer_3_out5[18]),
    .out9(demultiplexer_3_out5[10]), .out10(demultiplexer_3_out5[16]), .out11(demultiplexer_3_out5[2]),
    .out12(demultiplexer_3_out5[23]), .out13(demultiplexer_3_out5[4]), .out14(demultiplexer_3_out5[11]),
    .out15(demultiplexer_3_out5[8]), .out16(demultiplexer_3_out5[20]), .out17(demultiplexer_3_out5[13]),
    .out18(demultiplexer_3_out5[3]), .out19(demultiplexer_3_out5[22]), .out20(demultiplexer_3_out5[12]),
    .out21(demultiplexer_3_out5[1]), .out22(demultiplexer_3_out5[14]), .out23(demultiplexer_3_out5[17]),
    .out24(demultiplexer_3_out5[19]), .out25(demultiplexer_3_out5[6]), .out26(demultiplexer_3_out26),
    .out27(demultiplexer_3_out26), .out28(demultiplexer_3_out26), .out29(demultiplexer_3_out26),
    .out31(demultiplexer_3_out26), .in(INPUT_1), .sel(nextindex_backward_2_shift_index));  // open: out30
  Demultiplexer #(.select(5), .enable("false")) demultiplexer_4 (
    .out0(demultiplexer_4_out5[5]), .out1(demultiplexer_4_out5[21]), .out2(demultiplexer_4_out5[11]),
    .out3(demultiplexer_4_out5[18]), .out4(demultiplexer_4_out5[13]), .out5(demultiplexer_4_out5[0]),
    .out6(demultiplexer_4_out5[25]), .out7(demultiplexer_4_out5[4]), .out8(demultiplexer_4_out5[15]),
    .out9(demultiplexer_4_out5[1]), .out10(demultiplexer_4_out5[9]), .out11(demultiplexer_4_out5[14]),
    .out12(demultiplexer_4_out5[20]), .out13(demultiplexer_4_out5[17]), .out14(demultiplexer_4_out5[22]),
    .out15(demultiplexer_4_out5[3]), .out16(demultiplexer_4_out5[10]), .out17(demultiplexer_4_out5[23]),
    .out18(demultiplexer_4_out5[8]), .out19(demultiplexer_4_out5[24]), .out20(demultiplexer_4_out5[16]),
    .out21(demultiplexer_4_out5[6]), .out22(demultiplexer_4_out5[19]), .out23(demultiplexer_4_out5[12]),
    .out24(demultiplexer_4_out5[2]), .out25(demultiplexer_4_out5[7]), .out26(demultiplexer_4_out26),
    .out27(demultiplexer_4_out26), .out28(demultiplexer_4_out26), .out29(demultiplexer_4_out26),
    .out30(demultiplexer_4_out26), .out31(demultiplexer_4_out26), .in(INPUT_1),
    .sel(nextindex_forward_2_shift_index));
  BitFinder #(.width(26)) bitfinder_3 (.in(INPUT_26_LETTERS), .index(bitfinder_3_index));  // open: found
  BitFinder #(.width(26)) bitfinder_4 (.in(INPUT_26_LETTERS_2), .index(bitfinder_4_index));  // open: found
  NEXTINDEX_BACKWARD nextindex_backward_2 (
    .INPUT_ROTOR(ROTOR_POSITION), .SHIFT_INDEX(nextindex_backward_2_shift_index),
    .INPUT_INDEX(bitfinder_3_index));
  NEXTINDEX_FORWARD nextindex_forward_2 (
    .INPUT_INDEX(bitfinder_4_index), .INPUT_ROTOR(ROTOR_POSITION),
    .SHIFT_INDEX(nextindex_forward_2_shift_index));

  assign OUTPUT_1 = INPUT_1;

  // Other names for the same wires on the sheet: ROTORE[4:0] = ROTOR_POSITION

  // Notes on the sheet:
  //   FORWARD
  //   BACKWARD
  //   ROTOR-A
endmodule

module ROTOR_B (
  input  INPUT_1,
  input  [25:0] INPUT_26_LETTERS,
  input  [4:0] ROTOR_POSITION,
  input  [25:0] INPUT_26_LETTERS_2,
  output OUTPUT_1,
  output [25:0] OUTPUT_26_LETTERS,
  output [25:0] OUTPUT_26_LETTERS_2
);

  wire demultiplexer_1_out26, demultiplexer_2_out26, demultiplexer_3_out26, demultiplexer_4_out26;
  wire [4:0] bitfinder_1_index, bitfinder_2_index, bitfinder_3_index, bitfinder_4_index,
       nextindex_backward_1_shift_index, nextindex_backward_2_shift_index, nextindex_forward_1_shift_index,
       nextindex_forward_2_shift_index;
  wire [25:0] demultiplexer_3_out8, demultiplexer_4_out12;

  Demultiplexer #(.select(5), .enable("false")) demultiplexer_1 (
    .out0(OUTPUT_26_LETTERS[0]), .out1(OUTPUT_26_LETTERS[1]), .out2(OUTPUT_26_LETTERS[2]),
    .out3(OUTPUT_26_LETTERS[3]), .out4(OUTPUT_26_LETTERS[4]), .out5(OUTPUT_26_LETTERS[5]),
    .out6(OUTPUT_26_LETTERS[6]), .out7(OUTPUT_26_LETTERS[7]), .out8(OUTPUT_26_LETTERS[8]),
    .out9(OUTPUT_26_LETTERS[9]), .out10(OUTPUT_26_LETTERS[10]), .out11(OUTPUT_26_LETTERS[11]),
    .out12(OUTPUT_26_LETTERS[12]), .out13(OUTPUT_26_LETTERS[13]), .out14(OUTPUT_26_LETTERS[14]),
    .out15(OUTPUT_26_LETTERS[15]), .out16(OUTPUT_26_LETTERS[16]), .out17(OUTPUT_26_LETTERS[17]),
    .out18(OUTPUT_26_LETTERS[18]), .out19(OUTPUT_26_LETTERS[19]), .out20(OUTPUT_26_LETTERS[20]),
    .out21(OUTPUT_26_LETTERS[21]), .out22(OUTPUT_26_LETTERS[22]), .out23(OUTPUT_26_LETTERS[23]),
    .out24(OUTPUT_26_LETTERS[24]), .out25(OUTPUT_26_LETTERS[25]), .out26(demultiplexer_1_out26),
    .out27(demultiplexer_1_out26), .out28(demultiplexer_1_out26), .out29(demultiplexer_1_out26),
    .out30(demultiplexer_1_out26), .out31(demultiplexer_1_out26), .in(INPUT_1),
    .sel(nextindex_backward_1_shift_index));
  Demultiplexer #(.select(5), .enable("false")) demultiplexer_2 (
    .out0(OUTPUT_26_LETTERS_2[0]), .out1(OUTPUT_26_LETTERS_2[1]), .out2(OUTPUT_26_LETTERS_2[2]),
    .out3(OUTPUT_26_LETTERS_2[3]), .out4(OUTPUT_26_LETTERS_2[4]), .out5(OUTPUT_26_LETTERS_2[5]),
    .out6(OUTPUT_26_LETTERS_2[6]), .out7(OUTPUT_26_LETTERS_2[7]), .out8(OUTPUT_26_LETTERS_2[8]),
    .out9(OUTPUT_26_LETTERS_2[9]), .out10(OUTPUT_26_LETTERS_2[10]), .out11(OUTPUT_26_LETTERS_2[11]),
    .out12(OUTPUT_26_LETTERS_2[12]), .out13(OUTPUT_26_LETTERS_2[13]), .out14(OUTPUT_26_LETTERS_2[14]),
    .out15(OUTPUT_26_LETTERS_2[15]), .out16(OUTPUT_26_LETTERS_2[16]), .out17(OUTPUT_26_LETTERS_2[17]),
    .out18(OUTPUT_26_LETTERS_2[18]), .out19(OUTPUT_26_LETTERS_2[19]), .out20(OUTPUT_26_LETTERS_2[20]),
    .out21(OUTPUT_26_LETTERS_2[21]), .out22(OUTPUT_26_LETTERS_2[22]), .out23(OUTPUT_26_LETTERS_2[23]),
    .out24(OUTPUT_26_LETTERS_2[24]), .out25(OUTPUT_26_LETTERS_2[25]), .out26(demultiplexer_2_out26),
    .out27(demultiplexer_2_out26), .out28(demultiplexer_2_out26), .out29(demultiplexer_2_out26),
    .out30(demultiplexer_2_out26), .out31(demultiplexer_2_out26), .in(INPUT_1),
    .sel(nextindex_forward_1_shift_index));
  BitFinder #(.width(26)) bitfinder_1 (.in(demultiplexer_3_out8), .index(bitfinder_1_index));  // open: found
  NEXTINDEX_BACKWARD nextindex_backward_1 (
    .INPUT_ROTOR(ROTOR_POSITION), .SHIFT_INDEX(nextindex_backward_1_shift_index),
    .INPUT_INDEX(bitfinder_1_index));
  BitFinder #(.width(26)) bitfinder_2 (.in(demultiplexer_4_out12), .index(bitfinder_2_index));  // open: found
  NEXTINDEX_FORWARD nextindex_forward_1 (
    .INPUT_INDEX(bitfinder_2_index), .INPUT_ROTOR(ROTOR_POSITION),
    .SHIFT_INDEX(nextindex_forward_1_shift_index));
  Demultiplexer #(.select(5), .enable("false")) demultiplexer_3 (
    .out0(demultiplexer_3_out8[12]), .out1(demultiplexer_3_out8[4]), .out2(demultiplexer_3_out8[7]),
    .out3(demultiplexer_3_out8[25]), .out4(demultiplexer_3_out8[16]), .out5(demultiplexer_3_out8[10]),
    .out6(demultiplexer_3_out8[23]), .out7(demultiplexer_3_out8[14]), .out8(demultiplexer_3_out8[0]),
    .out9(demultiplexer_3_out8[6]), .out10(demultiplexer_3_out8[13]), .out11(demultiplexer_3_out8[3]),
    .out12(demultiplexer_3_out8[1]), .out13(demultiplexer_3_out8[24]), .out14(demultiplexer_3_out8[18]),
    .out15(demultiplexer_3_out8[21]), .out16(demultiplexer_3_out8[20]), .out17(demultiplexer_3_out8[2]),
    .out18(demultiplexer_3_out8[19]), .out19(demultiplexer_3_out8[5]), .out20(demultiplexer_3_out8[22]),
    .out21(demultiplexer_3_out8[17]), .out22(demultiplexer_3_out8[8]), .out23(demultiplexer_3_out8[15]),
    .out24(demultiplexer_3_out8[9]), .out25(demultiplexer_3_out8[11]), .out26(demultiplexer_3_out26),
    .out27(demultiplexer_3_out26), .out28(demultiplexer_3_out26), .out29(demultiplexer_3_out26),
    .out30(demultiplexer_3_out26), .out31(demultiplexer_3_out26), .in(INPUT_1),
    .sel(nextindex_backward_2_shift_index));
  Demultiplexer #(.select(5), .enable("false")) demultiplexer_4 (
    .out0(demultiplexer_4_out12[8]), .out1(demultiplexer_4_out12[12]), .out2(demultiplexer_4_out12[17]),
    .out3(demultiplexer_4_out12[11]), .out4(demultiplexer_4_out12[1]), .out5(demultiplexer_4_out12[19]),
    .out6(demultiplexer_4_out12[9]), .out7(demultiplexer_4_out12[2]), .out8(demultiplexer_4_out12[22]),
    .out9(demultiplexer_4_out12[24]), .out10(demultiplexer_4_out12[5]), .out11(demultiplexer_4_out12[25]),
    .out12(demultiplexer_4_out12[0]), .out13(demultiplexer_4_out12[10]), .out14(demultiplexer_4_out12[7]),
    .out15(demultiplexer_4_out12[23]), .out16(demultiplexer_4_out12[4]), .out17(demultiplexer_4_out12[21]),
    .out18(demultiplexer_4_out12[14]), .out19(demultiplexer_4_out12[18]), .out20(demultiplexer_4_out12[16]),
    .out21(demultiplexer_4_out12[15]), .out22(demultiplexer_4_out12[20]), .out23(demultiplexer_4_out12[6]),
    .out24(demultiplexer_4_out12[13]), .out25(demultiplexer_4_out12[3]), .out26(demultiplexer_4_out26),
    .out27(demultiplexer_4_out26), .out28(demultiplexer_4_out26), .out29(demultiplexer_4_out26),
    .out30(demultiplexer_4_out26), .out31(demultiplexer_4_out26), .in(INPUT_1),
    .sel(nextindex_forward_2_shift_index));
  NEXTINDEX_BACKWARD nextindex_backward_2 (
    .INPUT_ROTOR(ROTOR_POSITION), .SHIFT_INDEX(nextindex_backward_2_shift_index),
    .INPUT_INDEX(bitfinder_3_index));
  BitFinder #(.width(26)) bitfinder_3 (.in(INPUT_26_LETTERS), .index(bitfinder_3_index));  // open: found
  BitFinder #(.width(26)) bitfinder_4 (.in(INPUT_26_LETTERS_2), .index(bitfinder_4_index));  // open: found
  NEXTINDEX_FORWARD nextindex_forward_2 (
    .INPUT_INDEX(bitfinder_4_index), .INPUT_ROTOR(ROTOR_POSITION),
    .SHIFT_INDEX(nextindex_forward_2_shift_index));

  assign OUTPUT_1 = INPUT_1;

  // Other names for the same wires on the sheet: ROTORE[4:0] = ROTOR_POSITION

  // Notes on the sheet:
  //   FORWARD
  //   BACKWARD
  //   ROTOR-B
endmodule

module ROTOR_C (
  input  INPUT_1,
  input  [25:0] INPUT_26_LETTERS,
  input  [4:0] in_3,
  input  [25:0] INPUT_26_LETTERS_2,
  output OUTPUT_1,
  output [25:0] OUTPUT_26_LETTERS,
  output [25:0] OUTPUT_26_LETTERS_2
);

  wire demultiplexer_1_out26, demultiplexer_2_out26, demultiplexer_3_out26, demultiplexer_4_out26;
  wire [4:0] bitfinder_1_index, bitfinder_2_index, bitfinder_3_index, bitfinder_4_index,
       nextindex_backward_1_shift_index, nextindex_backward_2_shift_index, nextindex_forward_1_shift_index,
       nextindex_forward_2_shift_index;
  wire [25:0] demultiplexer_3_out0, demultiplexer_4_out23;

  Demultiplexer #(.select(5), .enable("false")) demultiplexer_1 (
    .out0(OUTPUT_26_LETTERS[0]), .out1(OUTPUT_26_LETTERS[1]), .out2(OUTPUT_26_LETTERS[2]),
    .out3(OUTPUT_26_LETTERS[3]), .out4(OUTPUT_26_LETTERS[4]), .out5(OUTPUT_26_LETTERS[5]),
    .out6(OUTPUT_26_LETTERS[6]), .out7(OUTPUT_26_LETTERS[7]), .out8(OUTPUT_26_LETTERS[8]),
    .out9(OUTPUT_26_LETTERS[9]), .out10(OUTPUT_26_LETTERS[10]), .out11(OUTPUT_26_LETTERS[11]),
    .out12(OUTPUT_26_LETTERS[12]), .out13(OUTPUT_26_LETTERS[13]), .out14(OUTPUT_26_LETTERS[14]),
    .out15(OUTPUT_26_LETTERS[15]), .out16(OUTPUT_26_LETTERS[16]), .out17(OUTPUT_26_LETTERS[17]),
    .out18(OUTPUT_26_LETTERS[18]), .out19(OUTPUT_26_LETTERS[19]), .out20(OUTPUT_26_LETTERS[20]),
    .out21(OUTPUT_26_LETTERS[21]), .out22(OUTPUT_26_LETTERS[22]), .out23(OUTPUT_26_LETTERS[23]),
    .out24(OUTPUT_26_LETTERS[24]), .out25(OUTPUT_26_LETTERS[25]), .out26(demultiplexer_1_out26),
    .out27(demultiplexer_1_out26), .out28(demultiplexer_1_out26), .out29(demultiplexer_1_out26),
    .out30(demultiplexer_1_out26), .out31(demultiplexer_1_out26), .in(INPUT_1),
    .sel(nextindex_backward_1_shift_index));
  Demultiplexer #(.select(5), .enable("false")) demultiplexer_2 (
    .out0(OUTPUT_26_LETTERS_2[0]), .out1(OUTPUT_26_LETTERS_2[1]), .out2(OUTPUT_26_LETTERS_2[2]),
    .out3(OUTPUT_26_LETTERS_2[3]), .out4(OUTPUT_26_LETTERS_2[4]), .out5(OUTPUT_26_LETTERS_2[5]),
    .out6(OUTPUT_26_LETTERS_2[6]), .out7(OUTPUT_26_LETTERS_2[7]), .out8(OUTPUT_26_LETTERS_2[8]),
    .out9(OUTPUT_26_LETTERS_2[9]), .out10(OUTPUT_26_LETTERS_2[10]), .out11(OUTPUT_26_LETTERS_2[11]),
    .out12(OUTPUT_26_LETTERS_2[12]), .out13(OUTPUT_26_LETTERS_2[13]), .out14(OUTPUT_26_LETTERS_2[14]),
    .out15(OUTPUT_26_LETTERS_2[15]), .out16(OUTPUT_26_LETTERS_2[16]), .out17(OUTPUT_26_LETTERS_2[17]),
    .out18(OUTPUT_26_LETTERS_2[18]), .out19(OUTPUT_26_LETTERS_2[19]), .out20(OUTPUT_26_LETTERS_2[20]),
    .out21(OUTPUT_26_LETTERS_2[21]), .out22(OUTPUT_26_LETTERS_2[22]), .out23(OUTPUT_26_LETTERS_2[23]),
    .out24(OUTPUT_26_LETTERS_2[24]), .out25(OUTPUT_26_LETTERS_2[25]), .out26(demultiplexer_2_out26),
    .out27(demultiplexer_2_out26), .out28(demultiplexer_2_out26), .out29(demultiplexer_2_out26),
    .out30(demultiplexer_2_out26), .out31(demultiplexer_2_out26), .in(INPUT_1),
    .sel(nextindex_forward_1_shift_index));
  NEXTINDEX_BACKWARD nextindex_backward_1 (
    .INPUT_ROTOR(in_3), .SHIFT_INDEX(nextindex_backward_1_shift_index), .INPUT_INDEX(bitfinder_1_index));
  BitFinder #(.width(26)) bitfinder_1 (.in(demultiplexer_3_out0), .index(bitfinder_1_index));  // open: found
  BitFinder #(.width(26)) bitfinder_2 (.in(demultiplexer_4_out23), .index(bitfinder_2_index));  // open: found
  NEXTINDEX_FORWARD nextindex_forward_1 (
    .INPUT_INDEX(bitfinder_2_index), .INPUT_ROTOR(in_3), .SHIFT_INDEX(nextindex_forward_1_shift_index));
  Demultiplexer #(.select(5), .enable("false")) demultiplexer_3 (
    .out0(demultiplexer_3_out0[23]), .out1(demultiplexer_3_out0[5]), .out2(demultiplexer_3_out0[9]),
    .out3(demultiplexer_3_out0[8]), .out4(demultiplexer_3_out0[4]), .out5(demultiplexer_3_out0[15]),
    .out6(demultiplexer_3_out0[6]), .out7(demultiplexer_3_out0[14]), .out8(demultiplexer_3_out0[7]),
    .out9(demultiplexer_3_out0[24]), .out10(demultiplexer_3_out0[0]), .out11(demultiplexer_3_out0[3]),
    .out12(demultiplexer_3_out0[10]), .out13(demultiplexer_3_out0[18]), .out14(demultiplexer_3_out0[20]),
    .out15(demultiplexer_3_out0[12]), .out16(demultiplexer_3_out0[25]), .out17(demultiplexer_3_out0[2]),
    .out18(demultiplexer_3_out0[21]), .out19(demultiplexer_3_out0[17]), .out20(demultiplexer_3_out0[1]),
    .out21(demultiplexer_3_out0[22]), .out22(demultiplexer_3_out0[11]), .out23(demultiplexer_3_out0[13]),
    .out24(demultiplexer_3_out0[19]), .out25(demultiplexer_3_out0[16]), .out26(demultiplexer_3_out26),
    .out27(demultiplexer_3_out26), .out28(demultiplexer_3_out26), .out29(demultiplexer_3_out26),
    .out30(demultiplexer_3_out26), .out31(demultiplexer_3_out26), .in(INPUT_1),
    .sel(nextindex_backward_2_shift_index));
  Demultiplexer #(.select(5), .enable("false")) demultiplexer_4 (
    .out0(demultiplexer_4_out23[10]), .out1(demultiplexer_4_out23[20]), .out2(demultiplexer_4_out23[17]),
    .out3(demultiplexer_4_out23[11]), .out4(demultiplexer_4_out23[4]), .out5(demultiplexer_4_out23[1]),
    .out6(demultiplexer_4_out23[6]), .out7(demultiplexer_4_out23[8]), .out8(demultiplexer_4_out23[3]),
    .out9(demultiplexer_4_out23[2]), .out10(demultiplexer_4_out23[12]), .out11(demultiplexer_4_out23[22]),
    .out12(demultiplexer_4_out23[15]), .out13(demultiplexer_4_out23[23]), .out14(demultiplexer_4_out23[7]),
    .out15(demultiplexer_4_out23[5]), .out16(demultiplexer_4_out23[25]), .out17(demultiplexer_4_out23[19]),
    .out18(demultiplexer_4_out23[13]), .out19(demultiplexer_4_out23[24]), .out20(demultiplexer_4_out23[14]),
    .out21(demultiplexer_4_out23[18]), .out22(demultiplexer_4_out23[21]), .out23(demultiplexer_4_out23[0]),
    .out24(demultiplexer_4_out23[9]), .out25(demultiplexer_4_out23[16]), .out26(demultiplexer_4_out26),
    .out27(demultiplexer_4_out26), .out28(demultiplexer_4_out26), .out29(demultiplexer_4_out26),
    .out30(demultiplexer_4_out26), .out31(demultiplexer_4_out26), .in(INPUT_1),
    .sel(nextindex_forward_2_shift_index));
  BitFinder #(.width(26)) bitfinder_3 (.in(INPUT_26_LETTERS), .index(bitfinder_3_index));  // open: found
  BitFinder #(.width(26)) bitfinder_4 (.in(INPUT_26_LETTERS_2), .index(bitfinder_4_index));  // open: found
  NEXTINDEX_BACKWARD nextindex_backward_2 (
    .INPUT_ROTOR(in_3), .SHIFT_INDEX(nextindex_backward_2_shift_index), .INPUT_INDEX(bitfinder_3_index));
  NEXTINDEX_FORWARD nextindex_forward_2 (
    .INPUT_INDEX(bitfinder_4_index), .INPUT_ROTOR(in_3), .SHIFT_INDEX(nextindex_forward_2_shift_index));

  assign OUTPUT_1 = INPUT_1;

  // Other names for the same wires on the sheet: ROTORE[4:0] = in_3

  // Notes on the sheet:
  //   FORWARD
  //   BACKWARD
  //   INPUT 
  //   ROTORE
  //   ROTOR-C
endmodule

module REFLECTOR (
  input  INPUT_1,
  input  [25:0] INPUT_26_LETTERS,
  output [25:0] OUTPUT_26_LETTERS
);

  wire demultiplexer_1_out26;
  wire [4:0] bitfinder_1_index;

  Demultiplexer #(.select(5), .enable("false")) demultiplexer_1 (
    .out0(OUTPUT_26_LETTERS[12]), .out1(OUTPUT_26_LETTERS[22]), .out2(OUTPUT_26_LETTERS[24]),
    .out3(OUTPUT_26_LETTERS[5]), .out4(OUTPUT_26_LETTERS[18]), .out5(OUTPUT_26_LETTERS[3]),
    .out6(OUTPUT_26_LETTERS[25]), .out7(OUTPUT_26_LETTERS[16]), .out8(OUTPUT_26_LETTERS[14]),
    .out9(OUTPUT_26_LETTERS[21]), .out10(OUTPUT_26_LETTERS[15]), .out11(OUTPUT_26_LETTERS[19]),
    .out12(OUTPUT_26_LETTERS[0]), .out13(OUTPUT_26_LETTERS[23]), .out14(OUTPUT_26_LETTERS[8]),
    .out15(OUTPUT_26_LETTERS[10]), .out16(OUTPUT_26_LETTERS[7]), .out17(OUTPUT_26_LETTERS[20]),
    .out18(OUTPUT_26_LETTERS[4]), .out19(OUTPUT_26_LETTERS[11]), .out20(OUTPUT_26_LETTERS[17]),
    .out21(OUTPUT_26_LETTERS[9]), .out22(OUTPUT_26_LETTERS[1]), .out23(OUTPUT_26_LETTERS[13]),
    .out24(OUTPUT_26_LETTERS[2]), .out25(OUTPUT_26_LETTERS[6]), .out26(demultiplexer_1_out26),
    .out27(demultiplexer_1_out26), .out28(demultiplexer_1_out26), .out29(demultiplexer_1_out26),
    .out30(demultiplexer_1_out26), .out31(demultiplexer_1_out26), .in(INPUT_1), .sel(bitfinder_1_index));
  BitFinder #(.width(26)) bitfinder_1 (.in(INPUT_26_LETTERS), .index(bitfinder_1_index));  // open: found

  // Notes on the sheet:
  //   REFLECTOR
endmodule

module NEXTINDEX_BACKWARD (
  input  [4:0] INPUT_INDEX,
  input  [4:0] INPUT_ROTOR,
  output [4:0] SHIFT_INDEX
);

  wire comparator_1_gt;
  wire [5:0] adder_1_out, bit_extender_1_out, bit_extender_2_out, subtractor_1_out;
  wire [5:5] multiplexer_1_out;

  assign bit_extender_1_out = {{1{1'b0}}, INPUT_INDEX};  // Bit_Extender bit_extender_1
  assign bit_extender_2_out = {{1{1'b0}}, INPUT_ROTOR};  // Bit_Extender bit_extender_2
  Adder #(.width(6)) adder_1 (.a(bit_extender_1_out), .b(bit_extender_2_out), .out(adder_1_out));  // open: cin, cout
  Comparator #(.width(6), .mode("unsigned")) comparator_1 (
    .a(adder_1_out), .b(6'b011001), .gt(comparator_1_gt));  // open: eq, lt
  Subtractor #(.width(6)) subtractor_1 (.a(adder_1_out), .b(6'b011010), .out(subtractor_1_out));  // open: bin, bout
  Multiplexer #(.width(6), .enable("false")) multiplexer_1 (
    .in0(adder_1_out), .in1(subtractor_1_out), .out({multiplexer_1_out[5], SHIFT_INDEX}),
    .sel(comparator_1_gt));
endmodule

module ENIGMA (
  input  A,
  input  B,
  input  C,
  input  [4:0] in_4,
  input  [4:0] in_5,
  input  [4:0] in_6,
  input  D,
  input  E,
  input  F,
  input  G,
  input  H,
  input  I,
  input  J,
  input  K,
  input  L,
  input  M,
  input  N,
  input  O,
  input  P,
  input  Q,
  input  R,
  input  S,
  input  S_2,
  input  U,
  input  V,
  input  W,
  input  in_27,
  input  X,
  input  Y,
  input  Z,
  output out_31,
  output out_32,
  output out_33,
  output out_34,
  output out_35,
  output out_36,
  output out_37,
  output out_38,
  output out_39,
  output out_40,
  output out_41,
  output out_42,
  output out_43,
  output out_44,
  output out_45,
  output out_46,
  output out_47,
  output out_48,
  output out_49,
  output out_50,
  output out_51,
  output out_52,
  output out_53,
  output out_54,
  output out_55,
  output out_56
);

  wire contatore_2_next_rotor_spin__1, contatore_3_next_rotor_spin__1, ONE, rotor_a_1_output_1,
       rotor_b_1_output_1, rotor_c_1_output_1;
  wire [4:0] contatore_1_rotor_position, contatore_2_rotor_position, contatore_3_rotor_position;
  wire [25:0] reflector_1_output_26_letters, rotor_a_1_output_26_letters, rotor_b_1_output_26_letters,
       rotor_b_1_output_26_letters_2, rotor_c_1_output_26_letters, rotor_c_1_output_26_letters_2;

  REFLECTOR reflector_1 (
    .INPUT_1(rotor_c_1_output_1), .INPUT_26_LETTERS(rotor_c_1_output_26_letters),
    .OUTPUT_26_LETTERS(reflector_1_output_26_letters));
  ROTOR_C rotor_c_1 (
    .OUTPUT_1(rotor_c_1_output_1), .INPUT_1(rotor_b_1_output_1), .in_3(contatore_1_rotor_position),
    .INPUT_26_LETTERS(rotor_b_1_output_26_letters), .OUTPUT_26_LETTERS(rotor_c_1_output_26_letters),
    .INPUT_26_LETTERS_2(reflector_1_output_26_letters), .OUTPUT_26_LETTERS_2(rotor_c_1_output_26_letters_2));
  CONTATORE contatore_1 (
    .WRITE(contatore_2_next_rotor_spin__1), .ROTOR_POSITION(contatore_1_rotor_position),
    .ROTOR_STARTING_POSITION(in_4), .INIT(in_27));  // open: NEXT_ROTOR_SPIN__1
  CONTATORE contatore_2 (
    .WRITE(contatore_3_next_rotor_spin__1), .ROTOR_POSITION(contatore_2_rotor_position),
    .NEXT_ROTOR_SPIN__1(contatore_2_next_rotor_spin__1), .ROTOR_STARTING_POSITION(in_5), .INIT(in_27));
  ROTOR_B rotor_b_1 (
    .OUTPUT_1(rotor_b_1_output_1), .INPUT_1(rotor_a_1_output_1),
    .INPUT_26_LETTERS(rotor_a_1_output_26_letters), .OUTPUT_26_LETTERS(rotor_b_1_output_26_letters),
    .INPUT_26_LETTERS_2(rotor_c_1_output_26_letters_2), .OUTPUT_26_LETTERS_2(rotor_b_1_output_26_letters_2),
    .ROTOR_POSITION(contatore_2_rotor_position));
  CONTATORE contatore_3 (
    .WRITE(ONE), .ROTOR_POSITION(contatore_3_rotor_position),
    .NEXT_ROTOR_SPIN__1(contatore_3_next_rotor_spin__1), .ROTOR_STARTING_POSITION(in_6), .INIT(in_27));
  ROTOR_A rotor_a_1 (
    .ROTOR_POSITION(contatore_3_rotor_position), .INPUT_1(ONE), .OUTPUT_1(rotor_a_1_output_1),
    .OUTPUT_26_LETTERS(rotor_a_1_output_26_letters),
    .INPUT_26_LETTERS({Z, Y, X, W, V, U, S_2, S, R, Q, P, O, N, M, L, K, J, I, H, G, F, E, D, C, B, A}),
    .INPUT_26_LETTERS_2(rotor_b_1_output_26_letters_2),
    .OUTPUT_26_LETTERS_2({out_56, out_55, out_54, out_53, out_52, out_51, out_50, out_49, out_48, out_47, out_46, out_45, out_44, out_43, out_42, out_41, out_40, out_39, out_38, out_37, out_36, out_35, out_34, out_33, out_32, out_31}));
  or or_1 (ONE, A, B, C, D, E, F, G, H, I, J, K, L, M, N, O, P, Q, R, S, S_2, U, V, W, X, Y, Z);

  // Other names for the same wires on the sheet: _7 = in_27;
  //   OUT[25:0] = {out_56, out_55, out_54, out_53, out_52, out_51, out_50, out_49, out_48, out_47, out_46, out_45, out_44, out_43, out_42, out_41, out_40, out_39, out_38, out_37, out_36, out_35, out_34, out_33, out_32, out_31}

  // Notes on the sheet:
  //   ENIGMA
endmodule

module CONTATORE (
  input  [4:0] ROTOR_STARTING_POSITION,
  input  INIT,
  input  WRITE,
  output [4:0] ROTOR_POSITION,
  output NEXT_ROTOR_SPIN__1
);

  wire and_1_out, and_3_out, comparator_1_gt, multiplexer_1_out, not_1_out, not_2_out;
  wire [4:0] adder_1_out, flip_flop_6_out_3, multiplexer_2_out, multiplexer_3_out;

  Multiplexer #(.enable("false")) multiplexer_1 (.in0(WRITE), .in1(INIT), .out(multiplexer_1_out), .sel(INIT));
  FLIP_FLOP flip_flop_1 (.in_1(multiplexer_3_out[4]), .in_2(multiplexer_1_out), .out_3(ROTOR_POSITION[4]));
  Adder #(.width(5)) adder_1 (.a(ROTOR_POSITION), .b(5'b00001), .out(adder_1_out));  // open: cin, cout
  FLIP_FLOP flip_flop_2 (.in_1(multiplexer_3_out[3]), .in_2(multiplexer_1_out), .out_3(ROTOR_POSITION[3]));
  Comparator #(.width(5), .mode("unsigned")) comparator_1 (
    .a(adder_1_out), .b(5'b11001), .gt(comparator_1_gt));  // open: eq, lt
  FLIP_FLOP flip_flop_3 (.in_1(multiplexer_3_out[2]), .in_2(multiplexer_1_out), .out_3(ROTOR_POSITION[2]));
  Multiplexer #(.width(5), .enable("false")) multiplexer_2 (
    .in0(adder_1_out), .in1({5{1'b0}}), .out(multiplexer_2_out), .sel(comparator_1_gt));
  FLIP_FLOP flip_flop_4 (.in_1(multiplexer_3_out[1]), .in_2(multiplexer_1_out), .out_3(ROTOR_POSITION[1]));
  not not_1 (not_1_out, INIT);
  and and_1 (and_1_out, ~multiplexer_3_out[4], ~multiplexer_3_out[3], ~multiplexer_3_out[2], ~multiplexer_3_out[1], ~multiplexer_3_out[0]);  // AND_Gate
  Multiplexer #(.width(5), .enable("false")) multiplexer_3 (
    .in0(ROTOR_STARTING_POSITION), .in1(flip_flop_6_out_3), .out(multiplexer_3_out), .sel(not_1_out));
  FLIP_FLOP flip_flop_5 (.in_1(multiplexer_3_out[0]), .in_2(multiplexer_1_out), .out_3(ROTOR_POSITION[0]));
  and and_2 (NEXT_ROTOR_SPIN__1, and_1_out, and_3_out);
  FLIP_FLOP flip_flop_6 (.in_1(multiplexer_2_out[0]), .in_2(not_2_out), .out_3(flip_flop_6_out_3[0]));
  not not_2 (not_2_out, multiplexer_1_out);
  FLIP_FLOP flip_flop_7 (.in_1(multiplexer_2_out[1]), .in_2(not_2_out), .out_3(flip_flop_6_out_3[1]));
  FLIP_FLOP flip_flop_8 (.in_1(multiplexer_2_out[2]), .in_2(not_2_out), .out_3(flip_flop_6_out_3[2]));
  FLIP_FLOP flip_flop_9 (.in_1(multiplexer_2_out[3]), .in_2(not_2_out), .out_3(flip_flop_6_out_3[3]));
  and and_3 (and_3_out, ~multiplexer_2_out[4], ~multiplexer_2_out[3], ~multiplexer_2_out[2], ~multiplexer_2_out[1], multiplexer_2_out[0]);  // AND_Gate
  FLIP_FLOP flip_flop_10 (.in_1(multiplexer_2_out[4]), .in_2(not_2_out), .out_3(flip_flop_6_out_3[4]));
endmodule

module ENIGMA_GUI (
  input  [4:0] in_1,
  input  [4:0] in_2,
  input  [4:0] in_3,
  input  W,
  input  in_5,
  input  in_6,
  input  in_7,
  input  in_8,
  input  in_9,
  input  in_10,
  input  in_11,
  input  in_12,
  input  in_13,
  input  in_14,
  input  in_15,
  input  in_16,
  input  in_17,
  input  in_18,
  input  in_19,
  input  in_20,
  input  in_21,
  input  in_22,
  input  in_23,
  input  in_24,
  input  in_25,
  input  in_26,
  input  in_27,
  input  in_28,
  input  in_29,
  input  in_30,
  output out_31,
  output out_32,
  output out_33,
  output out_34,
  output out_35,
  output out_36,
  output out_37,
  output out_38,
  output out_39,
  output out_40,
  output out_41,
  output out_42,
  output out_43,
  output out_44,
  output out_45,
  output out_46,
  output out_47,
  output out_48,
  output out_49,
  output out_50,
  output out_51,
  output out_52,
  output out_53,
  output out_54,
  output out_55,
  output out_56
);

  brown_color brown_color_1 ();
  brown_color brown_color_2 ();
  brown_color brown_color_3 ();
  brown_color brown_color_4 ();
  brown_color brown_color_5 ();
  brown_color brown_color_6 ();
  brown_color brown_color_7 ();
  brown_color brown_color_8 ();
  brown_color brown_color_9 ();
  brown_color brown_color_10 ();
  brown_color brown_color_11 ();
  brown_color brown_color_12 ();
  brown_color brown_color_13 ();
  brown_color brown_color_14 ();
  brown_color brown_color_15 ();
  brown_color brown_color_16 ();
  brown_color brown_color_17 ();
  brown_color brown_color_18 ();
  brown_color brown_color_19 ();
  brown_color brown_color_20 ();
  brown_color brown_color_21 ();
  brown_color brown_color_22 ();
  brown_color brown_color_23 ();
  brown_color brown_color_24 ();
  brown_color brown_color_25 ();
  brown_color brown_color_26 ();
  brown_color brown_color_27 ();
  brown_color brown_color_28 ();
  brown_color brown_color_29 ();
  brown_color brown_color_30 ();
  brown_color brown_color_31 ();
  brown_color brown_color_32 ();
  ENIGMA enigma_1 (
    .out_31(out_41), .out_32(out_54), .out_33(out_52), .out_34(out_43), .out_35(out_33), .out_36(out_44),
    .out_37(out_45), .out_38(out_46), .out_39(out_38), .out_40(out_47), .out_41(out_48), .out_42(out_49),
    .out_43(out_56), .out_44(out_55), .out_45(out_39), .out_46(out_40), .out_47(out_31), .out_48(out_34),
    .out_49(out_42), .out_50(out_35), .out_51(out_37), .out_52(out_53), .out_53(out_32), .in_27(W),
    .out_54(out_51), .out_55(out_36), .out_56(out_50), .A(in_15), .B(in_28), .C(in_26), .D(in_17), .E(in_7),
    .F(in_18), .G(in_19), .H(in_20), .I(in_12), .J(in_21), .K(in_22), .L(in_23), .M(in_30), .N(in_29),
    .O(in_13), .P(in_14), .Q(in_5), .R(in_8), .S(in_16), .S_2(in_9), .U(in_11), .V(in_27), .W(in_6),
    .X(in_25), .Y(in_10), .Z(in_24), .in_4(in_3), .in_5(in_2), .in_6(in_1));
  brown_color brown_color_33 ();
  brown_color brown_color_34 ();
  brown_color brown_color_35 ();
  brown_color brown_color_36 ();
  brown_color brown_color_37 ();
  brown_color brown_color_38 ();
  brown_color brown_color_39 ();
  brown_color brown_color_40 ();
  brown_color brown_color_41 ();
  brown_color brown_color_42 ();
  brown_color brown_color_43 ();
  brown_color brown_color_44 ();
  brown_color brown_color_45 ();
  brown_color brown_color_46 ();
  brown_color brown_color_47 ();
  brown_color brown_color_48 ();
  brown_color brown_color_49 ();
  brown_color brown_color_50 ();
  brown_color brown_color_51 ();
  brown_color brown_color_52 ();
  brown_color brown_color_53 ();
  brown_color brown_color_54 ();
  brown_color brown_color_55 ();
  brown_color brown_color_56 ();
  brown_color brown_color_57 ();
  brown_color brown_color_58 ();
  brown_color brown_color_59 ();
  brown_color brown_color_60 ();
  brown_color brown_color_61 ();
  brown_color brown_color_62 ();
  brown_color brown_color_63 ();
  brown_color brown_color_64 ();
  brown_color brown_color_65 ();
  brown_color brown_color_66 ();
  brown_color brown_color_67 ();
  brown_color brown_color_68 ();
  brown_color brown_color_69 ();
  brown_color brown_color_70 ();
  brown_color brown_color_71 ();
  brown_color brown_color_72 ();
  brown_color brown_color_73 ();
  brown_color brown_color_74 ();
  brown_color brown_color_75 ();
  brown_color brown_color_76 ();
  brown_color brown_color_77 ();
  brown_color brown_color_78 ();
  brown_color brown_color_79 ();
  brown_color brown_color_80 ();
  brown_color brown_color_81 ();
  brown_color brown_color_82 ();
  brown_color brown_color_83 ();
  brown_color brown_color_84 ();
  brown_color brown_color_85 ();
  brown_color brown_color_86 ();
  brown_color brown_color_87 ();
  brown_color brown_color_88 ();
  brown_color brown_color_89 ();
  brown_color brown_color_90 ();
  brown_color brown_color_91 ();

  // Other names for the same wires on the sheet: A = out_41; a_t = in_15; B = out_54; b_t = in_28; C = out_52;
  //   c_t = in_26; D = out_43; d_t = in_17; E = out_33; e_t = in_7; F = out_44; f_t = in_18; G = out_45; g_t = in_19;
  //   H = out_46; h_t = in_20; I = out_38; i_t = in_12; J = out_47; j_t = in_21; K = out_48; k_t = in_22; L = out_49;
  //   l_t = in_23; M = out_56; m_t = in_30; N = out_55; n_t = in_29; O = out_39; o_t = in_13; P = out_40; p_t = in_14;
  //   Q = out_31; q_t = in_5; R = out_34; r_t = in_8; S = out_42; s_t = in_16; T = out_35; t_t = in_9; U = out_37;
  //   u_t = in_11; V = out_53; v_t = in_27; W_t = out_32; w_t_t = in_6; X = out_51; x_t = in_25; Y = out_36;
  //   y_t = in_10; Z = out_50; z_t = in_24

  // Notes on the sheet:
  //   ENIGMA
endmodule
